# Fritzing sketch LCD-Stepper-Vend (saved by Fritzing 0.8.3b)
breadboards: 1

parts:
  Part2 = Arduino Uno (Rev3)
  BAT2 = BC9VPC [package=bc9vpc]
  M1 = Stepper Motor - Bipolar  # not connected
  U1 = LCD-16X2 [package=lcd-16x2]
  R1 = Resistor [tolerance=±5% resistance=220 package=THT]
  R2 = Trimmer Potentiometer [maximum_resistance=10kΩ package=THT]
  S1 = Pushbutton [package="[THT]"]
  R3 = Resistor [tolerance=±5% resistance=10k package=THT]
  LED5 = LED - 3mm [color="Red (633nm)" package="3 mm [THT]"]
  LED6 = LED - 3mm [color="Green (555nm)" package="3 mm [THT]"]

nets:
  N1: Part2.GND, BAT2.V+, U1.K
  N2: Part2.D12/MISO, U1.RS
  N3: Part2.D13/SCK, LED5.cathode
  N4: Part2.D1/TX, S1.Pin_1, S1.Pin_2, R3.Pin_0
  N5: Part2.D2, U1.DB7
  N6: Part2.D3_PWM, U1.DB6
  N7: Part2.D4, U1.DB5
  N8: Part2.D5_PWM, U1.DB4
  N9: Part2.D6_PWM, LED6.cathode
  N10: Part2.D7, U1.E
  N11: Part2.5V, R1.Pin_1
  N12: U1.VSS, U1.R_W, R2.leg1, R3.Pin_1, LED5.anode, LED6.anode
  N13: U1.VDD, R2.leg2, S1.Pin_3, S1.Pin_4
  N14: U1.VO, R2.wiper
  N15: U1.A, R1.Pin_0

notes:
  ULN2003 MOTOR DRIVER
  IN1 - IN2 - IN3 - IN4 - Neg - +5
  LED are not showing their resistors
